// Logisim project SquareRootV2_1.circ as structural Verilog: 5 circuits, main circuit main
module main (
  input  rst,
  output Ready,
  output [7:0] Final_Root
);

  wire clk, control_path_1_eninput, control_path_1_ensquare, control_path_1_ensum_2_root,
       control_path_1_muxroot_sum_2, control_path_1_muxsquare, control_path_1_opmux, data_path_1_menor,
       Start_out;
  wire [1:0] control_path_1_current_state;

  Clock u_clk (.out(clk));
  Button Start (.out(Start_out));
  Control_Path control_path_1 (
    .clk(clk), .rst(rst), .menor(data_path_1_menor), .start(Start_out),
    .MuxRoot_Sum_2(control_path_1_muxroot_sum_2), .enSum_2_Root(control_path_1_ensum_2_root),
    .MuxSquare(control_path_1_muxsquare), .enInput(control_path_1_eninput), .OpMux(control_path_1_opmux),
    .Current_State(control_path_1_current_state), .enSquare(control_path_1_ensquare));
  // Probe on control_path_1_current_state
  Data_Path data_path_1 (
    .\input (16'h10), .enInput(control_path_1_eninput), .root(8'h1), .Ready(Ready), .sum_2(16'h3),
    .square(16'h4), .Current_State(control_path_1_current_state),
    .Current_State_2(control_path_1_current_state), .clk(clk), .rst(rst),
    .MuxRoot_Sum_2(control_path_1_muxroot_sum_2), .enSum_2_Root(control_path_1_ensum_2_root),
    .MuxSquare(control_path_1_muxsquare), .enSquare(control_path_1_ensquare), .opMux(control_path_1_opmux),
    .menor(data_path_1_menor), .Final_Root(Final_Root));

  // Notes on the sheet:
  //   input
  //   root
  //   sum_2
  //   square
endmodule

module Data_Path (
  input  [15:0] \input ,
  input  enInput,
  input  [7:0] root,
  input  [1:0] Current_State,
  input  [15:0] sum_2,
  input  [1:0] Current_State_2,
  input  [15:0] square,
  input  opMux,
  input  enSquare,
  input  MuxSquare,
  input  clk,
  input  rst,
  input  MuxRoot_Sum_2,
  input  enSum_2_Root,
  output [7:0] Final_Root,
  output menor,
  output Ready
);

  wire and_1_out, and_2_out;
  wire [7:0] multiplexer_1_out, root_plus_plus;
  wire [15:0] input_q, multiplexer_2_out, multiplexer_3_out, multiplexer_4_out, square_q, sum_2_q, SumOut;

  Multiplexer #(.width(8), .enable("false")) multiplexer_1 (
    .in0(root), .in1(root_plus_plus), .out(multiplexer_1_out), .sel(MuxRoot_Sum_2));
  Multiplexer #(.width(16), .enable("false")) multiplexer_2 (
    .in0(sum_2), .in1(SumOut), .out(multiplexer_2_out), .sel(MuxRoot_Sum_2));
  Multiplexer #(.width(16), .enable("false")) multiplexer_3 (
    .in0(square), .in1(SumOut), .out(multiplexer_3_out), .sel(MuxSquare));
  Register #(.width(16)) u_input (.D(\input ), .en(enInput), .Q(input_q), .clk(clk), .clr(rst));
  Register u_root (.D(multiplexer_1_out), .en(enSum_2_Root), .Q(Final_Root), .clk(clk), .clr(rst));
  Register #(.width(16)) u_sum_2 (.D(multiplexer_2_out), .en(enSum_2_Root), .Q(sum_2_q), .clk(clk), .clr(rst));
  Register #(.width(16)) u_square (.D(multiplexer_3_out), .en(enSquare), .Q(square_q), .clk(clk), .clr(rst));
  Multiplexer #(.width(16), .enable("false")) multiplexer_4 (
    .in0(16'h2), .in1(square_q), .out(multiplexer_4_out), .sel(opMux));
  Comparator #(.width(16), .mode("unsigned")) comparator_1 (.a(input_q), .b(SumOut), .lt(menor));  // open: gt, eq
  Adder adder_1 (.a(Final_Root), .b(8'h1), .out(root_plus_plus));  // open: cin, cout
  Adder #(.width(16)) adder_2 (.a(sum_2_q), .b(multiplexer_4_out), .out(SumOut));  // open: cin, cout
  nor nor_1 (Ready, and_1_out, and_2_out);
  and and_1 (and_1_out, ~Current_State[0], Current_State[1], menor);  // AND_Gate
  and and_2 (and_2_out, Current_State_2[0], Current_State_2[1]);

  // Notes on the sheet:
  //   Ready output logic
endmodule

// OutPuts
module Outputs (
  input  Q1,
  input  Q0,
  output MuxRoot_Sum_2,
  output enSum_2_Root,
  output enSquare,
  output MuxSquare,
  output enInput,
  output OpMux
);

  wire not_3_out, not_4_out;

  not not_1 (enSum_2_Root, Q1);
  not not_2 (enSquare, Q0);
  not not_3 (not_3_out, Q1);
  not not_4 (not_4_out, Q0);
  not not_5 (OpMux, Q0);
  and and_1 (enInput, not_3_out, not_4_out);

  assign MuxRoot_Sum_2 = Q0;
  assign MuxSquare = Q1;
endmodule

module Next_State (
  input  Q1,
  input  Q0,
  input  rst,
  input  menor,
  input  start,
  output S1,
  output S0
);

  wire and_1_out, and_2_out, and_3_out, and_4_out, not_1_out, not_2_out, not_3_out, not_4_out, not_5_out;

  not not_1 (not_1_out, rst);
  not not_2 (not_2_out, rst);
  not not_3 (not_3_out, Q0);
  not not_4 (not_4_out, rst);
  not not_5 (not_5_out, rst);
  and and_1 (and_1_out, Q0, not_1_out);
  and and_2 (and_2_out, Q1, not_2_out, menor);
  and and_3 (and_3_out, not_3_out, not_4_out, start);
  and and_4 (and_4_out, Q1, not_5_out);
  or or_1 (S1, and_1_out, and_2_out);
  or or_2 (S0, and_3_out, and_4_out);
endmodule

module Control_Path (
  input  clk,
  input  rst,
  input  menor,
  input  start,
  output [1:0] Current_State,
  output MuxRoot_Sum_2,
  output enSum_2_Root,
  output enSquare,
  output MuxSquare,
  output enInput,
  output OpMux
);

  wire next_state_1_s0, next_state_1_s1;

  Next_State next_state_1 (
    .Q1(Current_State[1]), .Q0(Current_State[0]), .rst(rst), .menor(menor), .start(start),
    .S1(next_state_1_s1), .S0(next_state_1_s0));
  D_Flip_Flop S1 (.clk(clk), .D(next_state_1_s1), .Q(Current_State[1]), .reset(rst));  // open: Qn, preset, en
  D_Flip_Flop S0 (.clk(clk), .D(next_state_1_s0), .Q(Current_State[0]), .reset(rst));  // open: Qn, preset, en
  Outputs outputs_1 (
    .Q1(Current_State[1]), .Q0(Current_State[0]), .MuxRoot_Sum_2(MuxRoot_Sum_2), .enSum_2_Root(enSum_2_Root),
    .enSquare(enSquare), .MuxSquare(MuxSquare), .enInput(enInput), .OpMux(OpMux));
endmodule
