// Logisim project Odd_Even_sort.circ as structural Verilog: 6 circuits, main circuit main
module main (
  input  rst
);

  wire clk, control_path_1_eneven, control_path_1_muxeven, control_path_1_s0, data_path_1_even,
       data_path_1_sort, data_path_1_sorted, Start_out;
  wire [2:0] control_path_1_current_state;

  Clock u_clk (.out(clk));
  Data_Path data_path_1 (
    .V0(16'h1), .V1(16'h2), .V2(16'h6), .V3(16'h5), .V4(16'h4), .V5(16'h7), .V6(16'h8), .V7(16'ha),
    .V8(16'hb), .V9(16'h9), .Sorted(data_path_1_sorted), .CS(control_path_1_current_state),
    .MuexEven(control_path_1_muxeven), .enEven(control_path_1_eneven), .S0(control_path_1_s0), .clk(clk),
    .rst(rst), .Even(data_path_1_even), .sort(data_path_1_sort));
  // Probe on data_path_1_sorted
  // Probe on control_path_1_current_state
  Button Start (.out(Start_out));
  Control_Path control_path_1 (
    .start(Start_out), .even(data_path_1_even), .sort(data_path_1_sort), .S0(control_path_1_s0),
    .enEven(control_path_1_eneven), .MuxEven(control_path_1_muxeven),
    .Current_State(control_path_1_current_state), .clk(clk), .rst(rst));

  // Notes on the sheet:
  //   Keli Tauana Prass Ruppenthal
  //   Victor Dallagnol Bento
  //   Odd Even Sort Algorithm
endmodule

module Data_Path (
  input  [15:0] V0,
  input  [2:0] CS,
  input  MuexEven,
  input  enEven,
  input  S0,
  input  clk,
  input  rst,
  input  [15:0] V1,
  input  [15:0] V2,
  input  [15:0] V3,
  input  [15:0] V4,
  input  [15:0] V5,
  input  [15:0] V6,
  input  [15:0] V7,
  input  [15:0] V8,
  input  [15:0] V9,
  output Sorted,
  output sort,
  output Even
);

  wire d_ff_1_q, enV0, enV1, enV2, enV3, enV4, enV5, enV6, enV7, enV8, enV9, multiplexer_15_out, nor_1_out,
       nor_2_out, not_1_out, not_2_out, V0_t, V1_t, V2_t, V3_t, V4_t, V5_t, V6_t, V7_t, V8_t;
  wire [1:0] bit_extender_1_out, multiplexer_16_out, MuxRegs4;
  wire [15:0] _0, _1, _2, _3, _4, _5, _6, _7, _8, _9, multiplexer_1_out, multiplexer_2_out,
       multiplexer_3_out, multiplexer_4_out, multiplexer_5_out, multiplexer_6_out, multiplexer_7_out,
       multiplexer_8_out, multiplexer_9_out, multiplexer_10_out, multiplexer_11_out, multiplexer_12_out,
       multiplexer_13_out, multiplexer_14_out;

  Multiplexer #(.width(16), .enable("false")) multiplexer_1 (
    .in0(V0), .in1(_1), .out(multiplexer_1_out), .sel(not_1_out));
  not not_1 (not_1_out, S0);
  Multiplexer #(.select(2), .width(16), .enable("false")) multiplexer_2 (
    .in0(V1), .in1(_0), .in2(_2), .out(multiplexer_2_out), .sel(MuxRegs4));  // open: in3
  Multiplexer #(.select(2), .width(16), .enable("false")) multiplexer_3 (
    .in0(V2), .in1(_3), .in2(_1), .out(multiplexer_3_out), .sel(MuxRegs4));  // open: in3
  Multiplexer #(.select(2), .width(16), .enable("false")) multiplexer_4 (
    .in0(V3), .in1(_2), .in2(_4), .out(multiplexer_4_out), .sel(MuxRegs4));  // open: in3
  Multiplexer #(.select(2), .width(16), .enable("false")) multiplexer_5 (
    .in0(V4), .in1(_5), .in2(_3), .out(multiplexer_5_out), .sel(MuxRegs4));  // open: in3
  Multiplexer #(.select(2), .width(16), .enable("false")) multiplexer_6 (
    .in0(V5), .in1(_4), .in2(_6), .out(multiplexer_6_out), .sel(MuxRegs4));  // open: in3
  Multiplexer #(.select(2), .width(16), .enable("false")) multiplexer_7 (
    .in0(V6), .in1(_7), .in2(_5), .out(multiplexer_7_out), .sel(MuxRegs4));  // open: in3
  Multiplexer #(.select(2), .width(16), .enable("false")) multiplexer_8 (
    .in0(V7), .in1(_6), .in2(_8), .out(multiplexer_8_out), .sel(MuxRegs4));  // open: in3
  Multiplexer #(.select(2), .width(16), .enable("false")) multiplexer_9 (
    .in0(V8), .in1(_9), .in2(_7), .out(multiplexer_9_out), .sel(MuxRegs4));  // open: in3
  Multiplexer #(.width(16)) multiplexer_10 (.in0(V9), .in1(_8), .out(multiplexer_10_out), .sel(not_2_out));  // open: en
  not not_2 (not_2_out, S0);
  Register #(.width(16)) u_V0 (.D(multiplexer_1_out), .en(enV0), .Q(_0), .clk(clk), .clr(rst));
  Register #(.width(16)) u_V1 (.D(multiplexer_2_out), .en(enV1), .Q(_1), .clk(clk), .clr(rst));
  Register #(.width(16)) u_V2 (.D(multiplexer_3_out), .en(enV2), .Q(_2), .clk(clk), .clr(rst));
  Register #(.width(16)) u_V3 (.D(multiplexer_4_out), .en(enV3), .Q(_3), .clk(clk), .clr(rst));
  Register #(.width(16)) u_V4 (.D(multiplexer_5_out), .en(enV4), .Q(_4), .clk(clk), .clr(rst));
  Register #(.width(16)) u_V5 (.D(multiplexer_6_out), .en(enV5), .Q(_5), .clk(clk), .clr(rst));
  Register #(.width(16)) u_V6 (.D(multiplexer_7_out), .en(enV6), .Q(_6), .clk(clk), .clr(rst));
  Register #(.width(16)) u_V7 (.D(multiplexer_8_out), .en(enV7), .Q(_7), .clk(clk), .clr(rst));
  Register #(.width(16)) u_V8 (.D(multiplexer_9_out), .en(enV8), .Q(_8), .clk(clk), .clr(rst));
  Register #(.width(16)) u_V9 (.D(multiplexer_10_out), .en(enV9), .Q(_9), .clk(clk), .clr(rst));
  Multiplexer #(.width(16), .enable("false")) multiplexer_11 (.in0(_0), .in1(_2), .out(multiplexer_11_out), .sel(Even));
  Multiplexer #(.width(16), .enable("false")) multiplexer_12 (.in0(_2), .in1(_4), .out(multiplexer_12_out), .sel(Even));
  Multiplexer #(.width(16), .enable("false")) multiplexer_13 (.in0(_4), .in1(_6), .out(multiplexer_13_out), .sel(Even));
  Multiplexer #(.width(16), .enable("false")) multiplexer_14 (.in0(_6), .in1(_8), .out(multiplexer_14_out), .sel(Even));
  Comparator #(.width(16)) comparator_1 (.a(multiplexer_11_out), .b(_1), .gt(V0_t), .lt(V1_t));  // open: eq
  Comparator #(.width(16)) comparator_2 (.a(multiplexer_12_out), .b(_3), .gt(V2_t), .lt(V3_t));  // open: eq
  Comparator #(.width(16)) comparator_3 (.a(multiplexer_13_out), .b(_5), .gt(V4_t), .lt(V5_t));  // open: eq
  Comparator #(.width(16)) comparator_4 (.a(multiplexer_14_out), .b(_7), .gt(V6_t), .lt(V7_t));  // open: eq
  Comparator #(.width(16)) comparator_5 (.a(_8), .b(_9), .gt(V8_t));  // open: eq, lt
  Control_Register control_register_1 (
    .S0(S0), .Even(Even), .V0(V0_t), .V1(V1_t), .V2(V2_t), .V3(V3_t), .V4(V4_t), .V5(V5_t), .V6(V6_t),
    .V7(V7_t), .V8(V8_t), .en0(enV0), .en1(enV1), .en2(enV2), .en3(enV3), .en4(enV4), .en5(enV5), .en6(enV6),
    .en7(enV7), .en8(enV8), .en9(enV9));
  Multiplexer #(.enable("false")) multiplexer_15 (.in0(1'b0), .in1(1'b1), .out(multiplexer_15_out), .sel(MuexEven));
  Register #(.width(1)) u_Even (.D(multiplexer_15_out), .en(enEven), .Q(Even), .clk(clk), .clr(rst));
  nor nor_1 (nor_1_out, V0_t, V2_t, V4_t, V6_t, V8_t);
  D_Flip_Flop d_ff_1 (.clk(clk), .D(nor_2_out), .Q(d_ff_1_q), .en(Even), .reset(rst));  // open: Qn, preset
  nor nor_2 (nor_2_out, V1_t, V3_t, V5_t, V7_t);
  and and_1 (sort, nor_1_out, d_ff_1_q);
  Multiplexer #(.width(2), .enable("false")) multiplexer_16 (
    .in0(2'b01), .in1(2'b00), .out(multiplexer_16_out), .sel(S0));
  assign bit_extender_1_out = {{1{1'b0}}, Even};  // Bit_Extender bit_extender_1
  Adder #(.width(2)) adder_1 (.a(multiplexer_16_out), .b(bit_extender_1_out), .out(MuxRegs4));  // open: cin, cout
  and and_2 (Sorted, ~CS[0], ~CS[1], CS[2]);  // AND_Gate

  // Other names for the same wires on the sheet: Current_State[2:0] = CS; MuxEven = MuexEven; OddEven = Even

  // Notes on the sheet:
  //   V0>V1
  //   V1>V2
  //   V2>V3
  //   V3>V4
  //   V4>V5
  //   V5>V6
  //   V6>V7
  //   V7>V8
  //   V8>V9
  //   Verificação da ordenação do vetor
  //   Enable para os registradores
  //   Sinais
  //   Even = 0 e S0 = 1 : seleção 00
  //   Even = 0 e S0 = 0 : seleção 01
  //   Even = 1 e S0 = 0 : seleção 10
  //   Sorted
endmodule

module Control_Path (
  input  clk,
  input  rst,
  input  start,
  input  even,
  input  sort,
  output [2:0] Current_State,
  output S0,
  output enEven,
  output MuxEven
);

  wire next_state_1_s0, next_state_1_s1, next_state_1_s2;

  Next_State next_state_1 (
    .Q2(Current_State[2]), .Q1(Current_State[1]), .Q0(Current_State[0]), .rst(rst), .start(start),
    .even(even), .sort(sort), .S2(next_state_1_s2), .S1(next_state_1_s1), .S0(next_state_1_s0));
  D_Flip_Flop S2 (.clk(clk), .D(next_state_1_s2), .Q(Current_State[2]), .reset(rst));  // open: Qn, preset, en
  D_Flip_Flop S1 (.clk(clk), .D(next_state_1_s1), .Q(Current_State[1]), .reset(rst));  // open: Qn, preset, en
  D_Flip_Flop u_S0 (.clk(clk), .D(next_state_1_s0), .Q(Current_State[0]), .reset(rst));  // open: Qn, preset, en
  Output output_1 (
    .Q2(Current_State[2]), .Q1(Current_State[1]), .Q0(Current_State[0]), .S0(S0), .enEven(enEven),
    .MuxEven(MuxEven));
endmodule

// Outputs
module Output (
  input  Q2,
  input  Q1,
  input  Q0,
  output S0,
  output enEven,
  output MuxEven
);

  wire and_2_out, not_1_out, not_2_out, not_3_out, not_4_out, not_5_out, not_6_out;

  not not_1 (not_1_out, Q2);
  not not_2 (not_2_out, Q1);
  not not_3 (not_3_out, Q0);
  not not_4 (not_4_out, Q2);
  not not_5 (not_5_out, Q0);
  not not_6 (not_6_out, Q0);
  and and_1 (S0, not_1_out, not_2_out, not_3_out);
  and and_2 (and_2_out, not_4_out, not_5_out);
  and and_3 (MuxEven, Q1, not_6_out);
  or or_1 (enEven, and_2_out, Q1);
endmodule

module Next_State (
  input  Q2,
  input  Q1,
  input  Q0,
  input  rst,
  input  start,
  input  even,
  input  sort,
  output S2,
  output S1,
  output S0
);

  wire and_1_out, and_2_out, and_3_out, and_5_out, and_6_out, and_7_out, and_8_out, and_9_out, not_1_out,
       not_2_out, not_3_out, not_4_out, not_5_out, not_6_out, not_7_out, not_8_out, not_9_out, not_10_out,
       not_11_out, not_12_out, not_13_out, not_14_out, not_15_out, not_16_out, not_17_out, not_18_out;

  not not_1 (not_1_out, rst);
  not not_2 (not_2_out, Q0);
  not not_3 (not_3_out, rst);
  not not_4 (not_4_out, rst);
  not not_5 (not_5_out, Q2);
  not not_6 (not_6_out, Q1);
  not not_7 (not_7_out, rst);
  not not_8 (not_8_out, Q2);
  not not_9 (not_9_out, Q0);
  not not_10 (not_10_out, rst);
  not not_11 (not_11_out, Q2);
  not not_12 (not_12_out, rst);
  not not_13 (not_13_out, Q2);
  not not_14 (not_14_out, rst);
  not not_15 (not_15_out, Q0);
  not not_16 (not_16_out, rst);
  not not_17 (not_17_out, rst);
  not not_18 (not_18_out, sort);
  and and_1 (and_1_out, Q1, Q0, not_1_out);
  and and_2 (and_2_out, Q2, not_2_out, not_3_out);
  and and_3 (and_3_out, Q2, not_4_out, sort);
  and and_4 (S1, not_5_out, not_6_out, Q0, not_7_out);
  and and_5 (and_5_out, not_8_out, not_9_out, not_10_out, start);
  and and_6 (and_6_out, not_11_out, Q0, not_12_out, even);
  and and_7 (and_7_out, not_13_out, Q1, not_14_out);
  and and_8 (and_8_out, Q1, not_15_out, not_16_out);
  and and_9 (and_9_out, Q2, Q0, not_17_out, not_18_out);
  or or_1 (S2, and_1_out, and_2_out, and_3_out);
  or or_2 (S0, and_5_out, and_6_out, and_7_out, and_8_out, and_9_out);
endmodule

module Control_Register (
  input  S0,
  input  Even,
  input  V0,
  input  V1,
  input  V2,
  input  V3,
  input  V4,
  input  V5,
  input  V6,
  input  V7,
  input  V8,
  output en0,
  output en1,
  output en2,
  output en3,
  output en4,
  output en5,
  output en6,
  output en7,
  output en8,
  output en9
);

  wire and_1_out, and_2_out, and_3_out, and_4_out, and_5_out, and_6_out, and_7_out, and_8_out, and_9_out,
       and_10_out, and_11_out, and_12_out, and_13_out, and_14_out, and_15_out, and_16_out, and_17_out,
       and_18_out;

  and and_1 (and_1_out, ~Even, V0);  // AND_Gate
  and and_2 (and_2_out, ~Even, V0);  // AND_Gate
  and and_3 (and_3_out, Even, V1);
  and and_4 (and_4_out, ~Even, V2);  // AND_Gate
  and and_5 (and_5_out, Even, V1);
  and and_6 (and_6_out, ~Even, V2);  // AND_Gate
  and and_7 (and_7_out, Even, V3);
  and and_8 (and_8_out, ~Even, V4);  // AND_Gate
  and and_9 (and_9_out, Even, V3);
  and and_10 (and_10_out, ~Even, V4);  // AND_Gate
  and and_11 (and_11_out, Even, V5);
  and and_12 (and_12_out, ~Even, V6);  // AND_Gate
  and and_13 (and_13_out, Even, V5);
  and and_14 (and_14_out, ~Even, V6);  // AND_Gate
  and and_15 (and_15_out, Even, V7);
  and and_16 (and_16_out, ~Even, V8);  // AND_Gate
  and and_17 (and_17_out, Even, V7);
  and and_18 (and_18_out, ~Even, V8);  // AND_Gate
  or or_1 (en0, and_1_out, S0);
  or or_2 (en1, and_2_out, S0, and_3_out);
  or or_3 (en2, and_4_out, S0, and_5_out);
  or or_4 (en3, and_6_out, S0, and_7_out);
  or or_5 (en4, and_8_out, S0, and_9_out);
  or or_6 (en5, and_10_out, S0, and_11_out);
  or or_7 (en6, and_12_out, S0, and_13_out);
  or or_8 (en7, and_14_out, S0, and_15_out);
  or or_9 (en8, and_16_out, S0, and_17_out);
  or or_10 (en9, and_18_out, S0);
endmodule
