// Logisim project Square.circ as structural Verilog: 5 circuits, main circuit main
module main (
  input  in_1,
  input  [15:0] Input,
  input  [15:0] Root__1,
  input  [15:0] plus_1,
  input  [15:0] Sum_2__3,
  input  [15:0] plus_2,
  input  [15:0] Square__4,
  input  start,
  input  ready,
  output [2:0] Current_State,
  output ready_2,
  output menor,
  output [15:0] Final_Root
);

  wire clk, control_path_1_out_7, control_path_1_out_8, control_path_1_out_9, control_path_1_out_10,
       control_path_1_out_11, control_path_1_out_12, control_path_1_out_13;

  Control_Path control_path_1 (
    .in_1(in_1), .in_2(clk), .rst(in_1), .menor(menor), .start(start), .out_7(control_path_1_out_7),
    .out_8(control_path_1_out_8), .out_9(control_path_1_out_9), .out_10(control_path_1_out_10),
    .out_11(control_path_1_out_11), .out_12(control_path_1_out_12), .out_13(control_path_1_out_13),
    .Current_State(Current_State));
  Data_Path data_path_1 (
    .out_19(menor), .in_1(Input), .in_2(in_1), .in_3(clk), .enInput(control_path_1_out_7), .in_5(Root__1),
    .out_20(Final_Root), .in_6(plus_1), .in_7(control_path_1_out_11), .in_8(control_path_1_out_10),
    .in_9(Sum_2__3), .ready(ready), .out_21(ready_2), .enReady(control_path_1_out_8), .in_15(Square__4),
    .enSquare(control_path_1_out_9), .MuxSquare(control_path_1_out_12), .in_10(Current_State),
    .in_13(Current_State), .in_14(plus_2), .opMux(control_path_1_out_13));
  Clock clock_1 (.out(clk));

  // Other names for the same wires on the sheet: rst = in_1
endmodule

module Data_Path (
  input  [15:0] in_1,
  input  in_2,
  input  in_3,
  input  enInput,
  input  [15:0] in_5,
  input  [15:0] in_6,
  input  in_7,
  input  in_8,
  input  [15:0] in_9,
  input  [2:0] in_10,
  input  ready,
  input  enReady,
  input  [2:0] in_13,
  input  [15:0] in_14,
  input  [15:0] in_15,
  input  opMux,
  input  enSquare,
  input  MuxSquare,
  output out_19,
  output [15:0] out_20,
  output out_21
);

  wire and_1_out, and_2_out, and_3_out, condition, multiplexer_1_out, not_1_out;
  wire [15:0] adder_1_out, adder_2_out, input_q, multiplexer_2_out, multiplexer_3_out, multiplexer_4_out,
       multiplexer_5_out, multiplexer_6_out, square_q, sum_2_q;

  Multiplexer #(.enable("false")) multiplexer_1 (
    .in0(ready), .in1(not_1_out), .out(multiplexer_1_out), .sel(and_1_out));
  not not_1 (not_1_out, ready);
  and and_1 (and_1_out, out_19, ~in_2, condition);  // AND_Gate
  Multiplexer #(.width(16), .enable("false")) multiplexer_2 (
    .in0(in_5), .in1(adder_1_out), .out(multiplexer_2_out), .sel(in_7));
  Multiplexer #(.width(16), .enable("false")) multiplexer_3 (
    .in0(in_9), .in1(adder_2_out), .out(multiplexer_3_out), .sel(in_7));
  Multiplexer #(.width(16), .enable("false")) multiplexer_4 (
    .in0(in_15), .in1(adder_2_out), .out(multiplexer_4_out), .sel(MuxSquare));
  Register #(.width(16)) \input  (.D(in_1), .en(enInput), .Q(input_q), .clk(in_3), .clr(in_2));
  Register #(.width(16)) root (.D(multiplexer_2_out), .en(in_8), .Q(out_20), .clk(in_3), .clr(in_2));
  Register #(.width(16)) sum_2 (.D(multiplexer_3_out), .en(in_8), .Q(sum_2_q), .clk(in_3), .clr(in_2));
  Register #(.width(1)) u_ready (.D(multiplexer_1_out), .en(enReady), .Q(out_21), .clk(in_3), .clr(in_2));
  Register #(.width(16)) square (.D(multiplexer_4_out), .en(enSquare), .Q(square_q), .clk(in_3), .clr(in_2));
  Comparator #(.width(16)) comparator_1 (.a(input_q), .b(adder_2_out), .lt(out_19));  // open: gt, eq
  Adder #(.width(16)) adder_1 (.a(out_20), .b(in_6), .out(adder_1_out));  // open: cin, cout
  Multiplexer #(.width(16), .enable("false")) multiplexer_5 (
    .in0(in_14), .in1(sum_2_q), .out(multiplexer_5_out), .sel(opMux));
  Multiplexer #(.width(16), .enable("false")) multiplexer_6 (
    .in0(sum_2_q), .in1(square_q), .out(multiplexer_6_out), .sel(opMux));
  Adder #(.width(16)) adder_2 (.a(multiplexer_6_out), .b(multiplexer_5_out), .out(adder_2_out));  // open: cin, cout
  or or_1 (condition, and_2_out, and_3_out);
  and and_2 (and_2_out, ~in_10[0], ~in_10[1], in_10[2]);  // AND_Gate
  and and_3 (and_3_out, in_13[0], in_13[1], ~in_13[2]);  // AND_Gate

  // Other names for the same wires on the sheet: clk = in_3; enSum_2_Root = in_8; menor = out_19;
  //   MuxRoot_Sum_2 = in_7; rst = in_2
endmodule

module Control_Path (
  input  in_1,
  input  in_2,
  input  rst,
  input  menor,
  input  start,
  output [2:0] Current_State,
  output out_7,
  output out_8,
  output out_9,
  output out_10,
  output out_11,
  output out_12,
  output out_13
);

  wire next_state_1_s0, next_state_1_s1, next_state_1_s2;

  Next_State next_state_1 (
    .Q2(Current_State[2]), .S2(next_state_1_s2), .Q1(Current_State[1]), .Q0(Current_State[0]),
    .S1(next_state_1_s1), .rst(rst), .menor(menor), .start(start), .S0(next_state_1_s0));
  D_Flip_Flop S2 (.clk(in_2), .D(next_state_1_s2), .Q(Current_State[2]), .reset(in_1));  // open: Qn, preset, en
  D_Flip_Flop S1 (.clk(in_2), .D(next_state_1_s1), .Q(Current_State[1]), .reset(in_1));  // open: Qn, preset, en
  D_Flip_Flop S0 (.clk(in_2), .D(next_state_1_s0), .Q(Current_State[0]), .reset(in_1));  // open: Qn, preset, en
  Outputs outputs_1 (
    .Q2(Current_State[2]), .enInput(out_7), .Q1(Current_State[1]), .Q0(Current_State[0]), .enReady(out_8),
    .enSquare(out_9), .enSum_2_Root(out_10), .MuxRoot_Sum_2(out_11), .MuxSquare(out_12), .OpMux(out_13));

  // Other names for the same wires on the sheet: clk = in_2; rst_t = in_1
endmodule

module Next_State (
  input  Q2,
  input  Q1,
  input  Q0,
  input  rst,
  input  menor,
  input  start,
  output S2,
  output S1,
  output S0
);

  wire and_2_out, and_3_out, and_4_out, and_5_out, and_6_out, not_1_out, not_2_out, not_3_out, not_4_out,
       not_5_out, not_6_out, not_7_out, not_8_out, not_9_out, not_10_out, not_11_out, not_12_out, not_13_out;

  not not_1 (not_1_out, Q0);
  not not_2 (not_2_out, rst);
  not not_3 (not_3_out, menor);
  not not_4 (not_4_out, Q1);
  not not_5 (not_5_out, rst);
  not not_6 (not_6_out, Q0);
  not not_7 (not_7_out, rst);
  not not_8 (not_8_out, Q1);
  not not_9 (not_9_out, Q0);
  not not_10 (not_10_out, rst);
  not not_11 (not_11_out, Q0);
  not not_12 (not_12_out, rst);
  not not_13 (not_13_out, rst);
  and and_1 (S2, Q1, not_1_out, not_2_out, not_3_out);
  and and_2 (and_2_out, not_4_out, Q0, not_5_out);
  and and_3 (and_3_out, Q1, not_6_out, not_7_out, menor);
  and and_4 (and_4_out, not_8_out, not_9_out, not_10_out, start);
  and and_5 (and_5_out, Q1, not_11_out, not_12_out, menor);
  and and_6 (and_6_out, Q2, not_13_out);
  or or_1 (S1, and_2_out, and_3_out);
  or or_2 (S0, and_4_out, and_5_out, and_6_out);
endmodule

module Outputs (
  input  Q2,
  input  Q1,
  input  Q0,
  output enInput,
  output enReady,
  output enSquare,
  output enSum_2_Root,
  output MuxRoot_Sum_2,
  output MuxSquare,
  output OpMux
);

  wire and_2_out, and_3_out, not_1_out, not_2_out, not_3_out, not_4_out, not_5_out, not_6_out, not_7_out,
       not_8_out, not_9_out;

  not not_1 (not_1_out, Q2);
  not not_2 (not_2_out, Q1);
  not not_3 (not_3_out, Q0);
  not not_4 (not_4_out, Q1);
  not not_5 (not_5_out, Q0);
  not not_6 (not_6_out, Q2);
  not not_7 (not_7_out, Q0);
  not not_8 (not_8_out, Q2);
  not not_9 (not_9_out, Q1);
  not not_10 (OpMux, Q0);
  and and_1 (enInput, not_1_out, not_2_out, not_3_out);
  and and_2 (and_2_out, not_4_out, not_5_out);
  and and_3 (and_3_out, Q1, Q0);
  and and_4 (enSquare, not_6_out, not_7_out);
  and and_5 (enSum_2_Root, not_8_out, not_9_out);
  or or_1 (enReady, and_2_out, and_3_out);

  assign MuxRoot_Sum_2 = Q0;
  assign MuxSquare = Q1;
endmodule
